// Logisim project PKA08.circ as structural Verilog: 9 circuits, main circuit main
module main (
);

  wire a5min_1_b, a5min_1_lamp, a25min_1_b, a25min_1_lamp, and_1_out, and_2_out, clock_1_out, demux_1_out_3,
       demux_1_out_4, jk_1_q, lamp, MUX, mx_1_out_4, n7447_1_pin6, n7447_2_pin2, n7447_2_pin6, n7447_3_pin6,
       n7447_6_pin6, or_2_out, Reset_out, Start_Pause_out;
  wire [1:0] a25min_1_out_8;
  wire [2:0] a5min_1_detik1, a5min_1_menit, a25min_1_detik1;
  wire [3:0] a5min_1_detik0, a25min_1_detik0, a25min_1_menit0;
  wire [6:0] detik0, detik0_0, detik0_1, detik1, detik1_0, detik1_1, menit0, menit0_0, menit0_1, menit1;

  Button Reset (.out(Reset_out));
  Button Start_Pause (.out(Start_Pause_out));
  Clock clock_1 (.out(clock_1_out));
  JK jk_1 (.Q(jk_1_q), .J(1'b1), .K(1'b1), .C(Start_Pause_out));  // open: NQ
  MX mx_1 (.out_4(mx_1_out_4), .in_1(1'b0), .in_2(clock_1_out), .in_3(jk_1_q));
  or or_1 (lamp, a25min_1_lamp, and_2_out);
  and and_1 (and_1_out, mx_1_out_4, jk_1_q);
  DEMUX demux_1 (.out_3(demux_1_out_3), .out_4(demux_1_out_4), .in_1(MUX), .in_2(and_1_out));
  or or_2 (or_2_out, a5min_1_b, a25min_1_b);
  _7_Segment_Display u_7_segment_display_1 (
    .g(menit1[1]), .f(menit1[0]), .a(menit1[2]), .b(menit1[3]), .e(menit1[6]), .d(menit1[5]), .c(menit1[4]));  // open: dp
  _7_Segment_Display u_7_segment_display_2 (
    .g(menit0[1]), .f(menit0[0]), .a(menit0[2]), .b(menit0[3]), .e(menit0[6]), .d(menit0[5]), .c(menit0[4]));  // open: dp
  and and_2 (and_2_out, demux_1_out_4, a5min_1_lamp);
  LED led_1 (.in(and_2_out));
  LED led_2 (.in(lamp));
  _7_Segment_Display u_7_segment_display_3 (
    .g(detik1[1]), .f(detik1[0]), .a(detik1[2]), .b(detik1[3]), .e(detik1[6]), .d(detik1[5]), .c(detik1[4]));  // open: dp
  JK jk_2 (.Q(MUX), .J(1'b1), .K(1'b1), .C(or_2_out));  // open: NQ
  _7_Segment_Display u_7_segment_display_4 (
    .g(detik0[1]), .f(detik0[0]), .a(detik0[2]), .b(detik0[3]), .e(detik0[6]), .d(detik0[5]), .c(detik0[4]));  // open: dp
  a5min a5min_1 (
    .B(a5min_1_b), .menit(a5min_1_menit), .detik0(a5min_1_detik0), .detik1(a5min_1_detik1),
    .lamp(a5min_1_lamp), .A(demux_1_out_4), .FRst(Reset_out));
  a25min a25min_1 (
    .detik1(a25min_1_detik1), .B(a25min_1_b), .detik0(a25min_1_detik0), .out_8(a25min_1_out_8),
    .menit0(a25min_1_menit0), .lamp(a25min_1_lamp), .A(demux_1_out_3), .FRst(Reset_out));
  _7447 u_7447_1 (
    .pin1(a5min_1_menit[1]), .pin2(a5min_1_menit[2]), .pin6(n7447_1_pin6), .pin7(a5min_1_menit[0]),
    .pin15(menit0_0[0]), .pin14(menit0_0[1]), .pin13(menit0_0[2]), .pin12(menit0_0[3]), .pin11(menit0_0[4]),
    .pin10(menit0_0[5]), .pin9(menit0_0[6]));  // open: pin3, pin4, pin5
  _7447 u_7447_2 (
    .pin1(a25min_1_out_8[1]), .pin2(n7447_2_pin2), .pin6(n7447_2_pin6), .pin7(a25min_1_out_8[0]),
    .pin15(menit1[0]), .pin14(menit1[1]), .pin13(menit1[2]), .pin12(menit1[3]), .pin11(menit1[4]),
    .pin10(menit1[5]), .pin9(menit1[6]));  // open: pin3, pin4, pin5
  _7447 u_7447_3 (
    .pin1(a5min_1_detik1[1]), .pin2(a5min_1_detik1[2]), .pin6(n7447_3_pin6), .pin7(a5min_1_detik1[0]),
    .pin15(detik1_0[0]), .pin14(detik1_0[1]), .pin13(detik1_0[2]), .pin12(detik1_0[3]), .pin11(detik1_0[4]),
    .pin10(detik1_0[5]), .pin9(detik1_0[6]));  // open: pin3, pin4, pin5
  MX7 mx7_1 (.out_4(menit0), .in_1(menit0_1), .in_2(menit0_0), .in_3(MUX));
  _7447 u_7447_4 (
    .pin1(a25min_1_menit0[1]), .pin2(a25min_1_menit0[2]), .pin6(a25min_1_menit0[3]),
    .pin7(a25min_1_menit0[0]), .pin15(menit0_1[0]), .pin14(menit0_1[1]), .pin13(menit0_1[2]),
    .pin12(menit0_1[3]), .pin11(menit0_1[4]), .pin10(menit0_1[5]), .pin9(menit0_1[6]));  // open: pin3, pin4, pin5
  _7447 u_7447_5 (
    .pin1(a5min_1_detik0[1]), .pin2(a5min_1_detik0[2]), .pin6(a5min_1_detik0[3]), .pin7(a5min_1_detik0[0]),
    .pin15(detik0_0[0]), .pin14(detik0_0[1]), .pin13(detik0_0[2]), .pin12(detik0_0[3]), .pin11(detik0_0[4]),
    .pin10(detik0_0[5]), .pin9(detik0_0[6]));  // open: pin3, pin4, pin5
  MX7 mx7_2 (.out_4(detik1), .in_1(detik1_1), .in_2(detik1_0), .in_3(MUX));
  _7447 u_7447_6 (
    .pin1(a25min_1_detik1[1]), .pin2(a25min_1_detik1[2]), .pin6(n7447_6_pin6), .pin7(a25min_1_detik1[0]),
    .pin15(detik1_1[0]), .pin14(detik1_1[1]), .pin13(detik1_1[2]), .pin12(detik1_1[3]), .pin11(detik1_1[4]),
    .pin10(detik1_1[5]), .pin9(detik1_1[6]));  // open: pin3, pin4, pin5
  _7447 u_7447_7 (
    .pin1(a25min_1_detik0[1]), .pin2(a25min_1_detik0[2]), .pin6(a25min_1_detik0[3]),
    .pin7(a25min_1_detik0[0]), .pin15(detik0_1[0]), .pin14(detik0_1[1]), .pin13(detik0_1[2]),
    .pin12(detik0_1[3]), .pin11(detik0_1[4]), .pin10(detik0_1[5]), .pin9(detik0_1[6]));  // open: pin3, pin4, pin5
  MX7 mx7_3 (.out_4(detik0), .in_1(detik0_1), .in_2(detik0_0), .in_3(MUX));
  // also tied to GND on the sheet: {n7447_1_pin6, n7447_2_pin2, n7447_2_pin6, n7447_3_pin6, n7447_6_pin6}
endmodule

module D0 (
  input  A,
  input  Rst,
  input  FRst,
  output B,
  output s3,
  output s2,
  output s1,
  output s0
);

  wire and_1_out, and_2_out, or_1_out;

  J_K_Flip_Flop #(.trigger("falling")) j_k_ff_1 (
    .J(1'b1), .K(1'b1), .clk(A), .Q(s0), .reset(or_1_out));  // open: Qn, preset
  J_K_Flip_Flop #(.trigger("falling")) j_k_ff_2 (
    .J(1'b1), .K(1'b1), .clk(s0), .Q(s1), .reset(or_1_out));  // open: Qn, preset
  LED led_1 (.in(s3));
  LED led_2 (.in(s2));
  J_K_Flip_Flop #(.trigger("falling")) j_k_ff_3 (
    .J(1'b1), .K(1'b1), .clk(s1), .Q(s2), .reset(or_1_out));  // open: Qn, preset
  LED led_3 (.in(s1));
  LED led_4 (.in(s0));
  J_K_Flip_Flop #(.trigger("falling")) j_k_ff_4 (
    .J(1'b1), .K(1'b1), .clk(s2), .Q(s3), .reset(or_1_out));  // open: Qn, preset
  or or_1 (or_1_out, B, FRst);
  and and_1 (and_1_out, s0, s2);
  and and_2 (and_2_out, s1, s3);
  Multiplexer multiplexer_1 (.in0(and_2_out), .in1(and_1_out), .out(B), .sel(Rst));

  // Notes on the sheet:
  //   8
  //   4
  //   1
  //   2
endmodule

module D1 (
  input  A,
  input  FRst,
  output B,
  output s2,
  output s1,
  output s0
);

  wire or_1_out;

  J_K_Flip_Flop #(.trigger("falling")) j_k_ff_1 (
    .J(1'b1), .K(1'b1), .clk(A), .Q(s0), .reset(or_1_out));  // open: Qn, preset
  J_K_Flip_Flop #(.trigger("falling")) j_k_ff_2 (
    .J(1'b1), .K(1'b1), .clk(s0), .Q(s1), .reset(or_1_out));  // open: Qn, preset
  J_K_Flip_Flop #(.trigger("falling")) j_k_ff_3 (
    .J(1'b1), .K(1'b1), .clk(s1), .Q(s2), .reset(or_1_out));  // open: Qn, preset
  LED led_1 (.in(s2));
  LED led_2 (.in(s1));
  LED led_3 (.in(s0));
  and and_1 (B, s1, s2);
  or or_1 (or_1_out, B, FRst);

  // Notes on the sheet:
  //   4
  //   1
  //   2
endmodule

module a5min (
  input  A,
  input  FRst,
  output [3:0] detik0,
  output [2:0] detik1,
  output lamp,
  output B,
  output [2:0] menit
);

  wire and_1_out, and_3_out, clock_1_out, d0_1_b, d1_1_b, or_1_out;

  J_K_Flip_Flop #(.trigger("falling")) j_k_ff_1 (
    .J(1'b1), .K(1'b1), .clk(d1_1_b), .Q(menit[0]), .reset(or_1_out));  // open: Qn, preset
  J_K_Flip_Flop #(.trigger("falling")) j_k_ff_2 (
    .J(1'b1), .K(1'b1), .clk(menit[0]), .Q(menit[1]), .reset(or_1_out));  // open: Qn, preset
  D0 d0_1 (
    .A(A), .FRst(FRst), .B(d0_1_b), .s3(detik0[3]), .s2(detik0[2]), .s1(detik0[1]), .s0(detik0[0]));  // open: Rst
  D1 d1_1 (.s2(detik1[2]), .s1(detik1[1]), .s0(detik1[0]), .B(d1_1_b), .FRst(FRst), .A(d0_1_b));
  LED led_1 (.in(menit[2]));
  LED led_2 (.in(detik0[3]));
  LED led_3 (.in(detik0[2]));
  LED led_4 (.in(detik0[1]));
  LED led_5 (.in(detik0[0]));
  LED led_6 (.in(detik1[2]));
  LED led_7 (.in(detik1[1]));
  LED led_8 (.in(detik1[0]));
  J_K_Flip_Flop #(.trigger("falling")) j_k_ff_3 (
    .J(1'b1), .K(1'b1), .clk(menit[1]), .Q(menit[2]), .reset(or_1_out));  // open: Qn, preset
  or or_1 (or_1_out, FRst, B);
  LED led_9 (.in(menit[1]));
  LED led_10 (.in(menit[0]));
  and and_1 (and_1_out, detik1[2], detik1[0]);
  and and_2 (B, menit[0], menit[2]);
  and and_3 (and_3_out, and_1_out, menit[2]);
  T_Flip_Flop t_ff_1 (.T(and_3_out), .clk(clock_1_out), .Q(lamp));  // open: Qn, reset, preset
  Clock clock_1 (.out(clock_1_out));

  // Notes on the sheet:
  //   4
  //   2
  //   1
endmodule

module a25min (
  input  A,
  input  FRst,
  output [3:0] detik0,
  output [2:0] detik1,
  output [3:0] menit0,
  output lamp,
  output B,
  output [1:0] out_8
);

  wire and_1_out, and_3_out, clock_1_out, d0_1_b, d0_2_b, d1_1_b, or_1_out;

  J_K_Flip_Flop #(.trigger("falling")) j_k_ff_1 (
    .J(1'b1), .K(1'b1), .clk(d0_2_b), .Q(out_8[0]), .reset(or_1_out));  // open: Qn, preset
  J_K_Flip_Flop #(.trigger("falling")) j_k_ff_2 (
    .J(1'b1), .K(1'b1), .clk(out_8[0]), .Q(out_8[1]), .reset(or_1_out));  // open: Qn, preset
  D0 d0_1 (
    .A(A), .FRst(FRst), .B(d0_1_b), .s3(detik0[3]), .s2(detik0[2]), .s1(detik0[1]), .s0(detik0[0]));  // open: Rst
  LED led_1 (.in(detik0[3]));
  LED led_2 (.in(detik0[2]));
  LED led_3 (.in(detik0[1]));
  LED led_4 (.in(detik0[0]));
  D0 d0_2 (
    .A(d1_1_b), .Rst(out_8[1]), .FRst(FRst), .B(d0_2_b), .s3(menit0[3]), .s2(menit0[2]), .s1(menit0[1]),
    .s0(menit0[0]));
  LED led_5 (.in(out_8[1]));
  or or_1 (or_1_out, B, FRst);
  LED led_6 (.in(out_8[0]));
  LED led_7 (.in(menit0[3]));
  LED led_8 (.in(menit0[2]));
  LED led_9 (.in(menit0[1]));
  LED led_10 (.in(menit0[0]));
  and and_1 (and_1_out, and_3_out, menit0[2], out_8[1]);
  and and_2 (B, out_8[1], out_8[0]);
  D1 d1_1 (.s2(detik1[2]), .s1(detik1[1]), .s0(detik1[0]), .B(d1_1_b), .FRst(FRst), .A(d0_1_b));
  T_Flip_Flop t_ff_1 (.T(and_1_out), .clk(clock_1_out), .Q(lamp));  // open: Qn, reset, preset
  Clock clock_1 (.out(clock_1_out));
  LED led_11 (.in(detik1[2]));
  LED led_12 (.in(detik1[1]));
  LED led_13 (.in(detik1[0]));
  and and_3 (and_3_out, detik1[2], detik1[0]);

  // Notes on the sheet:
  //   2
  //   1
endmodule

module JK (
  input  J,
  input  K,
  input  C,
  output Q,
  output NQ
);

  wire nand_1_out, nand_2_out, nand_3_out, not_1_out;

  not not_1 (not_1_out, K);
  nand nand_1 (nand_1_out, NQ, J);
  nand nand_2 (nand_2_out, not_1_out, Q);
  D_Flip_Flop d_ff_1 (.D(nand_3_out), .clk(C), .Q(Q), .Qn(NQ));  // open: preset, reset
  nand nand_3 (nand_3_out, nand_1_out, nand_2_out);
endmodule

module DEMUX (
  input  in_1,
  input  in_2,
  output out_3,
  output out_4
);

  wire not_1_out;

  not not_1 (not_1_out, in_1);
  and and_1 (out_3, not_1_out, in_2);
  and and_2 (out_4, in_2, in_1);
endmodule

module MX (
  input  in_1,
  input  in_2,
  input  in_3,
  output out_4
);

  wire and_1_out, and_2_out, not_1_out;

  not not_1 (not_1_out, in_3);
  and and_1 (and_1_out, in_1, not_1_out);
  and and_2 (and_2_out, in_2, in_3);
  or or_1 (out_4, and_1_out, and_2_out);
endmodule

module MX7 (
  input  [6:0] in_1,
  input  [6:0] in_2,
  input  in_3,
  output [6:0] out_4
);

  wire not_1_out;
  wire [6:0] and_1_out, and_2_out, bit_extender_1_out, bit_extender_2_out;

  assign bit_extender_1_out = {{6{not_1_out}}, not_1_out};  // Bit_Extender bit_extender_1
  not not_1 (not_1_out, in_3);
  assign bit_extender_2_out = {{6{in_3}}, in_3};  // Bit_Extender bit_extender_2
  assign and_1_out = in_1 & bit_extender_1_out;  // AND_Gate and_1, 7 bits wide
  assign and_2_out = in_2 & bit_extender_2_out;  // AND_Gate and_2, 7 bits wide
  assign out_4 = and_1_out | and_2_out;  // OR_Gate or_1, 7 bits wide
endmodule
